# Fritzing sketch 기말프로젝트 (saved by Fritzing 0.9.3b)
breadboards: 1

parts:
  부품1 = LCD1602-I2C
  부품2 = Arduino Uno (Rev3)
  HC-SR04_Sensor_1 = HC-SR04 Ultrasonic Distance Sensor
  S1 = SWITCH-MOMENTARY-2 [package=tactile-pth-12mm]
  S2 = SWITCH-MOMENTARY-2 [package=tactile-pth-12mm]
  LED1 = LED - 5mm [color="Red (633nm)" package="5 mm [THT]"]

nets:
  GND: 부품1.GND, HC-SR04_Sensor_1.GND, S1.1, S2.1
  VCC: 부품1.VCC, 부품2.5V, HC-SR04_Sensor_1.VCC
  N1: 부품1.SDA, 부품2.A4/SDA
  N2: 부품1.SCL, 부품2.A5/SCL
  N3: 부품2.D11_PWM/MOSI, HC-SR04_Sensor_1.TRIG
  N4: 부품2.D12/MISO, HC-SR04_Sensor_1.ECHO
  N5: 부품2.D13/SCK, LED1.anode
  N6: 부품2.GND, LED1.cathode
  N7: 부품2.D3_PWM, S1.2

custom parts:
  LCD1602-I2C: A standard character display, usually with 2x16 characters. Comes in many colors with LCM1602 IIC attached.
